# Fritzing sketch Schaltplan (saved by Fritzing 0.9.2b)
breadboards: 1

parts:
  LED1 = smd LED [color="Red (633nm)" package="0805 [SMD]"]
  R1 = Resistor [tolerance=±5% resistance=220 package="2010 [SMD]"]
  Bauteil1 = Arduino Uno (Rev3)
  R2 = Resistor [tolerance=±5% resistance=220 package="2010 [SMD]"]
  LED2 = smd LED [color="Red (633nm)" package="0805 [SMD]"]
  Entfernungssensor = TSOP312.., 314.. [package=THT]

nets:
  N1: LED1.cathode, Bauteil1.GND, LED2.cathode, Entfernungssensor.Vs
  N2: LED1.anode, R1.Pin_0
  N3: R1.Pin_1, Bauteil1.D13/SCK
  N4: Bauteil1.A0, Entfernungssensor.GND
  N5: Bauteil1.D12/MISO, R2.Pin_1
  N6: Bauteil1.5V, Entfernungssensor.Data
  N7: R2.Pin_0, LED2.anode
